# Fritzing sketch template_fritzing(1) (saved by Fritzing 0.9.3b)
breadboards: 3

parts:
  JP1 = Header 12 [package=1x12_machine-pin-header_lock.004]
  JP2 = Header 12 [package=1x12_machine-pin-header_lock.004]
  J1 = Dagu DGServo 9g header connector (female) [package=THT]
  C1 = Capacitor Polarized [package=cpol-radial-10uf-25v]
  C2 = Capacitor Polarized [package=cpol-radial-10uf-25v]
  J2 = Dagu DGServo 9g header connector (female) [package=THT]
  J3 = Dagu DGServo 9g header connector (female) [package=THT]
  C3 = Ceramic Capacitor [capacitance=100nF package="100 mil [THT, multilayer]"]
  C4 = Ceramic Capacitor [capacitance=100nF package="100 mil [THT, multilayer]"]
  U1 = OP27 - Low Noise, Precision Op Amp [part_number=OP27]
  U2 = OP27 - Low Noise, Precision Op Amp [part_number=OP27]
  U3 = OP27 - Low Noise, Precision Op Amp [part_number=OP27]
  U4 = OP27 - Low Noise, Precision Op Amp [part_number=OP27]
  U5 = OP27 - Low Noise, Precision Op Amp [part_number=OP27]
  U6 = OP27 - Low Noise, Precision Op Amp [part_number=OP27]
  U7 = OP27 - Low Noise, Precision Op Amp [part_number=OP27]
  U8 = OP27 - Low Noise, Precision Op Amp [part_number=OP27]
  U9 = OP27 - Low Noise, Precision Op Amp [part_number=OP27]  # not connected
  U10 = OP27 - Low Noise, Precision Op Amp [part_number=OP27]  # not connected
  U11 = OP27 - Low Noise, Precision Op Amp [part_number=OP27]  # not connected
  U12 = OP27 - Low Noise, Precision Op Amp [part_number=OP27]  # not connected
  U13 = OP27 - Low Noise, Precision Op Amp [part_number=OP27]  # not connected
  R1 = Resistor [tolerance=±5% resistance=56k package=THT]
  R3 = Resistor [tolerance=±0.25% resistance=56k package=THT]
  R4 = Resistor [tolerance=±0.25% resistance=10k package=THT]
  R5 = Resistor [tolerance=±0.25% resistance=10k package=THT]
  R6 = TRIMPOT [package=3362u-2]
  C5 = Ceramic Capacitor [capacitance=100nF package="100 mil [THT, multilayer]"]
  C6 = Ceramic Capacitor [capacitance=100nF package="100 mil [THT, multilayer]"]
  C7 = Ceramic Capacitor [capacitance=100nF package="100 mil [THT, multilayer]"]
  C8 = Ceramic Capacitor [capacitance=100nF package="100 mil [THT, multilayer]"]
  C9 = Ceramic Capacitor [capacitance=100nF package="100 mil [THT, multilayer]"]
  C10 = Ceramic Capacitor [capacitance=100nF package="100 mil [THT, multilayer]"]
  R7 = Resistor [tolerance=±5% resistance=10k package=THT]
  R8 = Resistor [tolerance=±5% resistance=10k package=THT]
  R9 = Resistor [tolerance=±5% resistance=10k package=THT]
  R10 = Resistor [tolerance=±5% resistance=10k package=THT]
  C11 = Ceramic Capacitor [capacitance=100nF package="100 mil [THT, multilayer]"]
  C12 = Ceramic Capacitor [capacitance=100nF package="100 mil [THT, multilayer]"]
  R11 = Resistor [tolerance=±5% resistance=56k package=THT]
  R12 = Resistor [tolerance=±0.25% resistance=56k package=THT]
  R13 = Resistor [tolerance=±5% resistance=56k package=THT]
  C13 = Ceramic Capacitor [capacitance=100nF package="100 mil [THT, multilayer]"]
  C14 = Ceramic Capacitor [capacitance=100nF package="100 mil [THT, multilayer]"]
  C15 = Ceramic Capacitor [capacitance=100nF package="100 mil [THT, multilayer]"]
  C16 = Ceramic Capacitor [capacitance=100nF package="100 mil [THT, multilayer]"]
  C17 = Ceramic Capacitor [capacitance=100nF package="100 mil [THT, multilayer]"]
  C18 = Ceramic Capacitor [capacitance=100nF package="100 mil [THT, multilayer]"]
  R14 = Resistor [tolerance=±5% resistance=56k package=THT]
  R15 = Resistor [tolerance=±5% resistance=56k package=THT]
  R16 = Resistor [tolerance=±5% resistance=56k package=THT]
  R18 = TRIMPOT [package=3362u-2]
  C19 = Ceramic Capacitor [capacitance=100nF package="100 mil [THT, multilayer]"]
  J4 = Dagu DGServo 9g header connector (female) [package=THT]
  R19 = Resistor [tolerance=±5% resistance=56k package=THT]
  R20 = Resistor [tolerance=±5% resistance=56k package=THT]
  R21 = TRIMPOT [package=3362u-2]
  R22 = Resistor [tolerance=±5% resistance=56k package=THT]
  R23 = Resistor [tolerance=±5% resistance=56k package=THT]

nets:
  N1: JP1.1, JP2.1, C1.-
  N2: JP1.2, JP2.2, C1.+, C2.+, C3.0, C4.1, R3.Pin_1, C5.0, C6.0, C7.0, C8.1, C9.1, C10.1, R10.Pin_1
  N3: JP1.3, JP2.3, C2.-
  N4: JP1.4, JP2.4
  N5: JP1.5, JP2.5
  N6: JP1.6, JP2.6
  N7: JP1.7, JP2.7
  N8: JP1.8, JP2.8
  N9: JP1.9, JP2.9
  N10: JP1.10, JP2.10
  N11: JP1.11, JP2.11, J3.gnd
  N12: JP1.12, JP2.12, J2.gnd
  N13: J1.Vcc, R23.Pin_0
  N14: J2.Vcc, R5.Pin_0
  N15: J2.pulse, U3.+IN
  N16: J3.Vcc, R4.Pin_0
  N17: J3.pulse, U2.+IN
  N18: C3.1, U1.V+, U2.V+, U3.V+, U4.V+, C5.1, C6.1, C7.1
  N19: C4.0, U1.-V
  N20: U1.-IN, R1.Pin_1, R5.Pin_1
  N21: U1.+IN, R3.Pin_0, R4.Pin_1
  N22: U1.OUT, R1.Pin_0
  N23: U2.-IN, R6.WIPER, R8.Pin_1
  N24: U2.-V, U3.-V, U4.-V, C8.0, C9.0, C10.0
  N25: U2.OUT, U4.-IN, R8.Pin_0, R9.Pin_1
  N26: U3.-IN, R6.CCW, R7.Pin_1
  N27: U3.OUT, U4.+IN, R7.Pin_0, R10.Pin_0
  N28: U4.OUT, R9.Pin_0, R22.Pin_0
  N29: U5.-IN, R11.Pin_1, R22.Pin_1
  N30: U5.+IN, R12.Pin_0, R23.Pin_1
  N31: U5.-V, U6.-V, U7.-V, U8.-V, C12.0, C14.0, C16.0, C18.0
  N32: U5.OUT, R11.Pin_0, R14.Pin_0, R21.WIPER
  N33: U5.V+, U6.V+, U7.V+, U8.V+, C11.1, C13.1, C15.1, C17.1
  N34: U6.-IN, R13.Pin_1, R14.Pin_1
  N35: U6.+IN, U7.+IN, U8.+IN, C11.0, C12.1, R12.Pin_1, C13.0, C14.1, C15.0, C16.1, C17.0, C18.1, R21.CW
  N36: U6.OUT, R13.Pin_0, R15.Pin_0
  N37: U7.-IN, R15.Pin_1, R16.Pin_1, R19.Pin_1
  N38: U7.OUT, R18.WIPER
  N39: U7.TRIM#8, R18.CW
  N40: U8.-IN, C19.0, J4.gnd, R20.Pin_1
  N41: U8.OUT, C19.1, R19.Pin_0
  N42: R16.Pin_0, R18.CCW
  N43: R20.Pin_0, R21.CCW

notes:
  Fargekoding:
  Rød: V+
  Blå: V-
  Sort: GND
  Mal for Analog motorlab
  Kretsen kan også tegnes på papir eller ved bruk av andre programmer. Det som er viktig er at dere har en plan for hvordan dere skal koble kretsen når dere kommer på lab.
  TTK4101 Instrumentering og måleteknikk
  2018 Eivind H. Jølsgard
  V_out,
  V_m
